# Fritzing sketch tempyDAC (saved by Fritzing 0.9.3b)
circuit board: 8.46667cm x 5.64444cm
breadboards: 1

parts:
  ARD1 = Arduino Uno (Rev3)
  DS1 = DS18B20 1-Wire Temperature Sensor [part_number=DS18B20]
  R1 = Resistor [tolerance=±5% resistance=4.7k package=THT]
  U1 = MCP4725 [package=SOT23-6]
  U2 = Voltage Regulator [package=to220-adj]
  R2-36k = Resistor [tolerance=±5% resistance=33k package=THT]
  R3 = Resistor [tolerance=±1% resistance=330 package=THT]
  R4-7_6k = Resistor [tolerance=±5% resistance=6.8k package=THT]
  38V_EXT = Header 2 [package=jst-2-pth-ns]
  SIPMpol = Header 2 [package=molex-1x2_lock]
  Q2 = TRANSISTOR_NPN [package=to-92]

nets:
  N1: ARD1.A0, U1.AO
  N2: ARD1.A4/SDA, U1.SDA
  GND: ARD1.GND, DS1.GND, U1.VSS, R4-7_6k.Pin_1, 38V_EXT.2, SIPMpol.2, Q2.E
  N3: ARD1.A5/SCL, U1.SCL
  N4: ARD1.D2, DS1.DQ, R1.Pin_1
  VDD: ARD1.5V, DS1.VDD, R1.Pin_0, U1.VDD
  N5: U1.VOUT, Q2.B
  N6: U2.ADJ, R2-36k.Pin_1, R3.Pin_1, R4-7_6k.Pin_0
  N7: U2.IN, 38V_EXT.1
  N8: U2.OUT, R3.Pin_0, SIPMpol.1
  N9: R2-36k.Pin_0, Q2.C

notes:
  Vo=1.25(1+r2/r1)
  Vo=30V, si R1=330, R2=7590
  Vo=25V, si R1=330, R2=6270
  La variacion de R2 se obtiene del paralelo con otra Rc y un transistor.
  Luego R2=7590 y Rc=X. Como R2//Rc=6290
  Resulta Rc = 36k
